# Fritzing sketch panzer (saved by Fritzing 0.8.7b)
circuit board: 12cm x 6cm
breadboards: 1

parts:
  Componente1 = Relay T73
  Componente2 = Relay T73
  Componente3 = Relay T73
  Componente4 = Relay T73
  R1 = Resistor [tolerance=±5% resistance=220 package=THT]
  R2 = Resistor [tolerance=±5% resistance=220 package=THT]
  R3 = Resistor [tolerance=±5% resistance=220 package=THT]
  R4 = Resistor [tolerance=±5% resistance=220 package=THT]
  R5 = Resistor [tolerance=±5% resistance=220 package=THT]
  D1 = Rectifier Diode [part_number=1N4001 package="300 mil [THT]"]
  D2 = Rectifier Diode [part_number=1N4001 package="300 mil [THT]"]
  D3 = Rectifier Diode [part_number=1N4001 package="300 mil [THT]"]
  Q1 = Basic FET P-Channel [package="TO220 [THT]"]
  Q2 = Basic FET P-Channel [package="TO220 [THT]"]
  Q3 = PNP-Transistor [package="TO92 [THT]"]
  Q4 = PNP-Transistor [package="TO92 [THT]"]
  Q5 = PNP-Transistor [package="TO92 [THT]"]
  Componente5 = Relay T73

nets:
  N1: Componente1.C1, Componente2.C1, D1.anode, Q5.C
  N2: Componente1.C2, Componente2.C2, Componente3.C2, Componente4.C2, D1.cathode, D2.cathode, D3.cathode, Q1.source, Q2.source, Componente5.C2
  N3: Componente1.NO, Componente2.NC, Q2.drain
  N4: Componente1.NC, Componente2.NO, Componente3.NO, Componente4.NC, Componente5.NC
  N5: Componente3.C1, D2.anode, Q4.C, Componente5.C1
  N6: Componente3.NC, Q1.drain, Componente5.NO
  N7: Componente4.C1, D3.anode, Q3.C
  N8: Componente4.COM, Q3.E, Q4.E, Q5.E
  N9: R1.Pin_1, Q1.gate
  N10: R2.Pin_1, Q2.gate
  N11: R3.Pin_1, Q5.B
  N12: R4.Pin_1, Q3.B
  N13: R5.Pin_1, Q4.B

notes:
  +
  -

custom parts:
  Relay T73: An T73 Mini PCB Relay
